# Fritzing sketch scheme (saved by Fritzing 0.9.3b)
breadboards: 1

parts:
  Componente1 = Arduino Nano (Rev3.0) (ICSP)
  M1 = NRF24L01-BO [package=THT]

nets:
  N1: Componente1.RESET, Componente1.D7
  GND: Componente1.GND, M1.GND
  N2: Componente1.D9, M1.CE
  N3: Componente1.D10, M1.CSN
  N4: Componente1.D11/MOSI, M1.M0
  N5: Componente1.D12/MISO, M1.M1
  5V: Componente1.5V, M1.VCC
  N6: Componente1.D13/SCK, M1.SCK

custom parts:
  NRF24L01-BO: NRF24L01-BO breakout board for the NRF24L01. Pcb view suppressed as unneeded.
